// Logisim project lab4_prelab.circ as structural Verilog: 2 circuits, main circuit full-adder
module full_adder (
  input  C_IN,
  input  A,
  input  B,
  output S,
  output C_out
);

  wire and_1_out, and_2_out, xor_1_out;

  xor xor_1 (xor_1_out, A, B);
  and and_1 (and_1_out, B, A);
  and and_2 (and_2_out, xor_1_out, C_IN);
  xor xor_2 (S, C_IN, xor_1_out);
  or or_1 (C_out, and_2_out, and_1_out);
endmodule

module _8bit (
  input  A,
  input  in_2,
  input  in_3,
  input  in_4,
  input  in_5,
  input  in_6,
  input  in_7,
  input  in_8,
  input  CTRL,
  input  in_10,
  input  in_11,
  input  in_12,
  input  in_13,
  input  in_14,
  input  in_15,
  input  in_16,
  input  in_17,
  output out_18,
  output out_19,
  output out_20,
  output out_21,
  output out_22,
  output out_23,
  output out_24,
  output out_25,
  output C_OUT
);

  wire full_adder_1_c_out, full_adder_2_c_out, full_adder_3_c_out, full_adder_4_c_out, full_adder_5_c_out,
       full_adder_6_c_out, full_adder_7_c_out, xor_1_out, xor_2_out, xor_3_out, xor_4_out, xor_5_out,
       xor_6_out, xor_7_out, xor_8_out;

  xor xor_1 (xor_1_out, CTRL, in_10);
  xor xor_2 (xor_2_out, CTRL, in_11);
  xor xor_3 (xor_3_out, CTRL, in_12);
  xor xor_4 (xor_4_out, CTRL, in_13);
  xor xor_5 (xor_5_out, CTRL, in_14);
  xor xor_6 (xor_6_out, CTRL, in_15);
  xor xor_7 (xor_7_out, CTRL, in_16);
  xor xor_8 (xor_8_out, CTRL, in_17);
  full_adder full_adder_1 (.C_IN(CTRL), .A(A), .B(xor_1_out), .S(out_18), .C_out(full_adder_1_c_out));
  full_adder full_adder_2 (.C_IN(full_adder_1_c_out), .A(in_2), .B(xor_2_out), .S(out_19), .C_out(full_adder_2_c_out));
  full_adder full_adder_3 (.C_IN(full_adder_2_c_out), .A(in_3), .B(xor_3_out), .S(out_20), .C_out(full_adder_3_c_out));
  full_adder full_adder_4 (.C_IN(full_adder_3_c_out), .A(in_4), .B(xor_4_out), .S(out_21), .C_out(full_adder_4_c_out));
  full_adder full_adder_5 (.C_IN(full_adder_4_c_out), .A(in_5), .B(xor_5_out), .S(out_22), .C_out(full_adder_5_c_out));
  full_adder full_adder_6 (.C_IN(full_adder_5_c_out), .A(in_6), .B(xor_6_out), .S(out_23), .C_out(full_adder_6_c_out));
  full_adder full_adder_7 (.C_IN(full_adder_6_c_out), .A(in_7), .B(xor_7_out), .S(out_24), .C_out(full_adder_7_c_out));
  full_adder full_adder_8 (.C_IN(full_adder_7_c_out), .A(in_8), .B(xor_8_out), .S(out_25), .C_out(C_OUT));

  // Notes on the sheet:
  //   B
endmodule
