// Logisim project lab5_prelab.circ as structural Verilog: 2 circuits, main circuit main
module main (
  input  [3:0] A,
  input  [3:0] B,
  output [7:0] S
);

  wire and_1_out, and_2_out, and_3_out, and_4_out, and_5_out, and_6_out, and_7_out, and_8_out, and_9_out,
       and_10_out, and_11_out, and_12_out, and_13_out, and_14_out, and_15_out, n4bit_fa_2_co, n4bit_fa_3_co,
       n4bit_fa_3_s, n4bit_fa_4_co, n4bit_fa_5_co, n4bit_fa_5_s, n4bit_fa_6_co, n4bit_fa_6_s, n4bit_fa_7_co,
       n4bit_fa_8_co, n4bit_fa_8_s, n4bit_fa_9_co, n4bit_fa_9_s, n4bit_fa_10_co, n4bit_fa_11_co,
       n4bit_fa_11_s, n4bit_fa_12_co;

  and and_1 (and_1_out, B[3], A[3]);
  _4bit_fa u_4bit_fa_1 (.A(n4bit_fa_3_co), .B(and_1_out), .Ci(n4bit_fa_2_co), .S(S[6]), .Co(S[7]));
  and and_2 (and_2_out, B[3], A[2]);
  _4bit_fa u_4bit_fa_2 (.A(n4bit_fa_3_s), .B(and_2_out), .Ci(n4bit_fa_4_co), .S(S[5]), .Co(n4bit_fa_2_co));
  and and_3 (and_3_out, B[2], A[3]);
  _4bit_fa u_4bit_fa_3 (.A(n4bit_fa_6_co), .B(and_3_out), .Ci(n4bit_fa_5_co), .S(n4bit_fa_3_s), .Co(n4bit_fa_3_co));
  and and_4 (and_4_out, B[3], A[1]);
  and and_5 (and_5_out, B[2], A[2]);
  _4bit_fa u_4bit_fa_4 (.A(n4bit_fa_5_s), .B(and_4_out), .Ci(n4bit_fa_7_co), .S(S[4]), .Co(n4bit_fa_4_co));
  and and_6 (and_6_out, B[1], A[3]);
  _4bit_fa u_4bit_fa_5 (.A(n4bit_fa_6_s), .B(and_5_out), .Ci(n4bit_fa_8_co), .S(n4bit_fa_5_s), .Co(n4bit_fa_5_co));
  _4bit_fa u_4bit_fa_6 (.A(1'b0), .B(and_6_out), .Ci(n4bit_fa_9_co), .S(n4bit_fa_6_s), .Co(n4bit_fa_6_co));
  and and_7 (and_7_out, B[3], A[0]);
  and and_8 (and_8_out, B[2], A[1]);
  _4bit_fa u_4bit_fa_7 (.A(n4bit_fa_8_s), .B(and_7_out), .Ci(1'b0), .S(S[3]), .Co(n4bit_fa_7_co));
  and and_9 (and_9_out, B[1], A[2]);
  _4bit_fa u_4bit_fa_8 (.A(n4bit_fa_9_s), .B(and_8_out), .Ci(n4bit_fa_10_co), .S(n4bit_fa_8_s), .Co(n4bit_fa_8_co));
  and and_10 (and_10_out, B[0], A[3]);
  _4bit_fa u_4bit_fa_9 (.A(and_10_out), .B(and_9_out), .Ci(n4bit_fa_11_co), .S(n4bit_fa_9_s), .Co(n4bit_fa_9_co));
  and and_11 (and_11_out, B[2], A[0]);
  _4bit_fa u_4bit_fa_10 (.A(n4bit_fa_11_s), .B(and_11_out), .Ci(1'b0), .S(S[2]), .Co(n4bit_fa_10_co));
  and and_12 (and_12_out, B[1], A[1]);
  _4bit_fa u_4bit_fa_11 (.A(and_13_out), .B(and_12_out), .Ci(n4bit_fa_12_co), .S(n4bit_fa_11_s), .Co(n4bit_fa_11_co));
  and and_13 (and_13_out, B[0], A[2]);
  and and_14 (and_14_out, B[1], A[0]);
  _4bit_fa u_4bit_fa_12 (.A(and_15_out), .B(and_14_out), .Ci(1'b0), .S(S[1]), .Co(n4bit_fa_12_co));
  and and_15 (and_15_out, B[0], A[1]);
  and and_16 (S[0], B[0], A[0]);
endmodule

module _4bit_fa (
  input  A,
  input  B,
  input  Ci,
  output S,
  output Co
);

  wire and_1_out, and_2_out, and_3_out, xor_1_out;

  xor xor_1 (xor_1_out, A, B);
  and and_1 (and_1_out, B, A);
  and and_2 (and_2_out, Ci, A);
  and and_3 (and_3_out, Ci, B);
  xor xor_2 (S, xor_1_out, Ci);
  or or_1 (Co, and_1_out, and_2_out, and_3_out);
endmodule
